// Logisim project 32bit adder.circ as structural Verilog: 1 circuit, main circuit main
module main (
  input  in_1,
  input  in_2,
  input  in_3,
  input  in_4,
  input  in_5,
  input  in_6,
  input  in_7,
  input  in_8,
  input  in_9,
  input  in_10,
  input  in_11,
  input  in_12,
  input  in_13,
  input  in_14,
  input  in_15,
  input  in_16,
  input  in_17,
  input  in_18,
  input  in_19,
  input  in_20,
  input  in_21,
  input  in_22,
  input  in_23,
  input  in_24,
  input  in_25,
  input  in_26,
  input  in_27,
  input  in_28,
  input  in_29,
  input  in_30,
  input  in_31,
  input  in_32,
  input  in_33,
  input  in_34,
  input  in_35,
  input  in_36,
  input  in_37,
  input  in_38,
  input  in_39,
  input  in_40,
  input  in_41,
  input  in_42,
  input  in_43,
  input  in_44,
  input  in_45,
  input  in_46,
  input  in_47,
  input  in_48,
  input  in_49,
  input  in_50,
  input  in_51,
  input  in_52,
  input  in_53,
  input  in_54,
  input  in_55,
  input  in_56,
  input  in_57,
  input  in_58,
  input  in_59,
  input  in_60,
  input  in_61,
  input  in_62,
  input  in_63,
  input  in_64,
  input  in_65,
  input  in_66
);

  wire adder_1_cout, adder_1_out, adder_2_cout, adder_2_out, adder_3_cout, adder_3_out, adder_4_cout,
       adder_4_out, adder_5_cout, adder_5_out, adder_6_cout, adder_6_out, adder_7_cout, adder_7_out,
       adder_8_cout, adder_8_out, adder_9_cout, adder_9_out, adder_10_cout, adder_10_out, adder_11_cout,
       adder_11_out, adder_12_cout, adder_12_out, adder_13_cout, adder_13_out, adder_14_cout, adder_14_out,
       adder_15_cout, adder_15_out, adder_16_cout, adder_16_out, adder_17_cout, adder_17_out, adder_18_cout,
       adder_18_out, adder_19_cout, adder_19_out, adder_20_cout, adder_20_out, adder_21_cout, adder_21_out,
       adder_22_cout, adder_22_out, adder_23_cout, adder_23_out, adder_24_cout, adder_24_out, adder_25_cout,
       adder_25_out, adder_26_cout, adder_26_out, adder_27_cout, adder_27_out, adder_28_cout, adder_28_out,
       adder_29_cout, adder_29_out, adder_30_cout, adder_30_out, adder_31_cout, adder_31_out, adder_32_cout,
       adder_32_out, xor_1_out, xor_2_out, xor_3_out, xor_4_out, xor_5_out, xor_6_out, xor_7_out, xor_8_out,
       xor_9_out, xor_10_out, xor_11_out, xor_12_out, xor_13_out, xor_14_out, xor_15_out, xor_16_out,
       xor_17_out, xor_18_out, xor_19_out, xor_20_out, xor_21_out, xor_22_out, xor_23_out, xor_24_out,
       xor_25_out, xor_26_out, xor_27_out, xor_28_out, xor_29_out, xor_30_out, xor_31_out, xor_32_out,
       xor_33_out, xor_34_out;

  xor xor_1 (xor_1_out, in_3, in_1);
  xor xor_2 (xor_2_out, in_4, in_1);
  xor xor_3 (xor_3_out, in_6, in_1);
  xor xor_4 (xor_4_out, in_8, in_1);
  xor xor_5 (xor_5_out, in_10, in_1);
  xor xor_6 (xor_6_out, in_12, in_1);
  xor xor_7 (xor_7_out, in_14, in_1);
  xor xor_8 (xor_8_out, in_16, in_1);
  xor xor_9 (xor_9_out, in_18, in_1);
  xor xor_10 (xor_10_out, in_20, in_1);
  xor xor_11 (xor_11_out, in_22, in_1);
  xor xor_12 (xor_12_out, in_24, in_1);
  xor xor_13 (xor_13_out, in_26, in_1);
  xor xor_14 (xor_14_out, in_28, in_1);
  xor xor_15 (xor_15_out, in_30, in_1);
  xor xor_16 (xor_16_out, in_32, in_1);
  xor xor_17 (xor_17_out, in_34, in_1);
  xor xor_18 (xor_18_out, in_36, in_1);
  xor xor_19 (xor_19_out, in_38, in_1);
  xor xor_20 (xor_20_out, in_40, in_1);
  xor xor_21 (xor_21_out, in_42, in_1);
  xor xor_22 (xor_22_out, in_44, in_1);
  xor xor_23 (xor_23_out, in_46, in_1);
  xor xor_24 (xor_24_out, in_48, in_1);
  xor xor_25 (xor_25_out, in_50, in_1);
  xor xor_26 (xor_26_out, in_52, in_1);
  xor xor_27 (xor_27_out, in_54, in_1);
  xor xor_28 (xor_28_out, in_56, in_1);
  xor xor_29 (xor_29_out, in_58, in_1);
  xor xor_30 (xor_30_out, in_60, in_1);
  xor xor_31 (xor_31_out, in_62, in_1);
  xor xor_32 (xor_32_out, in_64, in_1);
  xor xor_33 (xor_33_out, in_66, in_1);
  LED led_1 (.in(adder_1_out));
  Adder #(.width(1)) adder_1 (.a(in_2), .b(xor_2_out), .out(adder_1_out), .cin(xor_1_out), .cout(adder_1_cout));
  LED led_2 (.in(adder_2_out));
  Adder #(.width(1)) adder_2 (.a(in_5), .b(xor_3_out), .out(adder_2_out), .cin(adder_1_cout), .cout(adder_2_cout));
  Adder #(.width(1)) adder_3 (.a(in_7), .b(xor_4_out), .out(adder_3_out), .cin(adder_2_cout), .cout(adder_3_cout));
  LED led_3 (.in(adder_3_out));
  LED led_4 (.in(adder_4_out));
  Adder #(.width(1)) adder_4 (.a(in_9), .b(xor_5_out), .out(adder_4_out), .cin(adder_3_cout), .cout(adder_4_cout));
  LED led_5 (.in(adder_5_out));
  Adder #(.width(1)) adder_5 (.a(in_11), .b(xor_6_out), .out(adder_5_out), .cin(adder_4_cout), .cout(adder_5_cout));
  Adder #(.width(1)) adder_6 (.a(in_13), .b(xor_7_out), .out(adder_6_out), .cin(adder_5_cout), .cout(adder_6_cout));
  LED led_6 (.in(adder_6_out));
  Adder #(.width(1)) adder_7 (.a(in_15), .b(xor_8_out), .out(adder_7_out), .cin(adder_6_cout), .cout(adder_7_cout));
  LED led_7 (.in(adder_7_out));
  Adder #(.width(1)) adder_8 (.a(in_17), .b(xor_9_out), .out(adder_8_out), .cin(adder_7_cout), .cout(adder_8_cout));
  LED led_8 (.in(adder_8_out));
  LED led_9 (.in(adder_9_out));
  Adder #(.width(1)) adder_9 (.a(in_19), .b(xor_10_out), .out(adder_9_out), .cin(adder_8_cout), .cout(adder_9_cout));
  LED led_10 (.in(adder_10_out));
  Adder #(.width(1)) adder_10 (.a(in_21), .b(xor_11_out), .out(adder_10_out), .cin(adder_9_cout), .cout(adder_10_cout));
  Adder #(.width(1)) adder_11 (
    .a(in_23), .b(xor_12_out), .out(adder_11_out), .cin(adder_10_cout), .cout(adder_11_cout));
  LED led_11 (.in(adder_11_out));
  LED led_12 (.in(adder_12_out));
  Adder #(.width(1)) adder_12 (
    .a(in_25), .b(xor_13_out), .out(adder_12_out), .cin(adder_11_cout), .cout(adder_12_cout));
  Adder #(.width(1)) adder_13 (
    .a(in_27), .b(xor_14_out), .out(adder_13_out), .cin(adder_12_cout), .cout(adder_13_cout));
  LED led_13 (.in(adder_13_out));
  Adder #(.width(1)) adder_14 (
    .a(in_29), .b(xor_15_out), .out(adder_14_out), .cin(adder_13_cout), .cout(adder_14_cout));
  LED led_14 (.in(adder_14_out));
  LED led_15 (.in(adder_15_out));
  Adder #(.width(1)) adder_15 (
    .a(in_31), .b(xor_16_out), .out(adder_15_out), .cin(adder_14_cout), .cout(adder_15_cout));
  Adder #(.width(1)) adder_16 (
    .a(in_33), .b(xor_17_out), .out(adder_16_out), .cin(adder_15_cout), .cout(adder_16_cout));
  LED led_16 (.in(adder_16_out));
  LED led_17 (.in(adder_17_out));
  Adder #(.width(1)) adder_17 (
    .a(in_35), .b(xor_18_out), .out(adder_17_out), .cin(adder_16_cout), .cout(adder_17_cout));
  LED led_18 (.in(adder_18_out));
  Adder #(.width(1)) adder_18 (
    .a(in_37), .b(xor_19_out), .out(adder_18_out), .cin(adder_17_cout), .cout(adder_18_cout));
  Adder #(.width(1)) adder_19 (
    .a(in_39), .b(xor_20_out), .out(adder_19_out), .cin(adder_18_cout), .cout(adder_19_cout));
  LED led_19 (.in(adder_19_out));
  LED led_20 (.in(adder_20_out));
  Adder #(.width(1)) adder_20 (
    .a(in_41), .b(xor_21_out), .out(adder_20_out), .cin(adder_19_cout), .cout(adder_20_cout));
  LED led_21 (.in(adder_21_out));
  Adder #(.width(1)) adder_21 (
    .a(in_43), .b(xor_22_out), .out(adder_21_out), .cin(adder_20_cout), .cout(adder_21_cout));
  Adder #(.width(1)) adder_22 (
    .a(in_45), .b(xor_23_out), .out(adder_22_out), .cin(adder_21_cout), .cout(adder_22_cout));
  LED led_22 (.in(adder_22_out));
  LED led_23 (.in(adder_23_out));
  Adder #(.width(1)) adder_23 (
    .a(in_47), .b(xor_24_out), .out(adder_23_out), .cin(adder_22_cout), .cout(adder_23_cout));
  Adder #(.width(1)) adder_24 (
    .a(in_49), .b(xor_25_out), .out(adder_24_out), .cin(adder_23_cout), .cout(adder_24_cout));
  LED led_24 (.in(adder_24_out));
  LED led_25 (.in(adder_25_out));
  Adder #(.width(1)) adder_25 (
    .a(in_51), .b(xor_26_out), .out(adder_25_out), .cin(adder_24_cout), .cout(adder_25_cout));
  LED led_26 (.in(adder_26_out));
  Adder #(.width(1)) adder_26 (
    .a(in_53), .b(xor_27_out), .out(adder_26_out), .cin(adder_25_cout), .cout(adder_26_cout));
  Adder #(.width(1)) adder_27 (
    .a(in_55), .b(xor_28_out), .out(adder_27_out), .cin(adder_26_cout), .cout(adder_27_cout));
  LED led_27 (.in(adder_27_out));
  LED led_28 (.in(adder_28_out));
  Adder #(.width(1)) adder_28 (
    .a(in_57), .b(xor_29_out), .out(adder_28_out), .cin(adder_27_cout), .cout(adder_28_cout));
  LED led_29 (.in(adder_29_out));
  Adder #(.width(1)) adder_29 (
    .a(in_59), .b(xor_30_out), .out(adder_29_out), .cin(adder_28_cout), .cout(adder_29_cout));
  LED led_30 (.in(adder_30_out));
  Adder #(.width(1)) adder_30 (
    .a(in_61), .b(xor_31_out), .out(adder_30_out), .cin(adder_29_cout), .cout(adder_30_cout));
  LED led_31 (.in(adder_31_out));
  Adder #(.width(1)) adder_31 (
    .a(in_63), .b(xor_32_out), .out(adder_31_out), .cin(adder_30_cout), .cout(adder_31_cout));
  Adder #(.width(1)) adder_32 (
    .a(in_65), .b(xor_33_out), .out(adder_32_out), .cin(adder_31_cout), .cout(adder_32_cout));
  LED led_32 (.in(adder_32_out));
  xor xor_34 (xor_34_out, adder_32_cout, in_1);
  LED led_33 (.in(xor_34_out));
endmodule
